# Fritzing sketch Level_Sensor_v2 (saved by Fritzing 0.9.3b)
circuit board: 7.46194cm x 3.64177cm
breadboards: 1

parts:
  Arduino_Nano = Arduino Nano (Rev3.0)
  FRS1B-S = Relay [part_number=FRS1B-S package=THT]
  R1-560 = Resistor [tolerance=±5% resistance=560 package=THT]
  D1 = Rectifier Diode [part_number=1N4148 package="300 mil [THT]"]
  A2 = Dagu DGServo 9g header (male) [package=THT]
  A3 = Dagu DGServo 9g header (male) [package=THT]
  LM7805 = Voltage Regulator - 5V [part_number=LM7805 package="TO220 [THT]"]
  A1 = Dagu DGServo 9g header (male) [package=THT]
  220µF = Electrolytic Capacitor [capacitance=100µF package="200 mil [THT, electrolytic]"]
  LED1 = LED - 3mm [color="Blue (525nm)" package="3 mm [THT]"]
  R2-470 = Resistor [tolerance=±5% resistance=470 package=THT]
  JP1 = Header 2 [part_number=JP1-12V package=screwterminal-3.5mm-2_lock]
  D2 = Rectifier Diode [part_number=1N4148 package="300 mil [THT]"]
  BC548C = NPN-Transistor [package="TO92 [THT]"]
  D3 = Rectifier Diode [part_number=1N4148 package="300 mil [THT]"]
  JP2 = Header 2 [package=screwterminal-3.5mm-2_lock]

nets:
  GND: Arduino_Nano.GND, A2.gnd, A3.gnd, LM7805.GND, A1.gnd, 220µF.-, R2-470.Pin_1, JP1.2, BC548C.E, JP2.2
  N1: Arduino_Nano.D2, R1-560.Pin_0
  VCC: Arduino_Nano.5V, FRS1B-S.COIL2, D1.cathode, A2.Vcc, A3.Vcc, LM7805.output_voltage, A1.Vcc, 220µF.+, D2.anode
  N2: Arduino_Nano.A3, A3.pulse
  N3: Arduino_Nano.A2, A2.pulse
  N4: Arduino_Nano.A1, A1.pulse
  N5: FRS1B-S.COIL1, D1.anode, BC548C.C
  N6: FRS1B-S.C1, FRS1B-S.C2, JP1.1, D3.anode
  N7: FRS1B-S.B, LED1.anode, JP2.1
  N8: R1-560.Pin_1, BC548C.B
  N9: LM7805.input_voltage, D2.cathode, D3.cathode
  N10: LED1.cathode, R2-470.Pin_0

notes:
  Level Sensor
  (c) H.Waiczies
  v2 01.2019
  D1, D2, D3 = 1N4148
  +  -
  12V
  Pump
  -  +  S
  A1 = Water Tank Level Low
  A2 = Aquarium Level Low
  A3 = Aquarium Level High
  A1 disable: 1k S to +
  A3 disable: 1k S to -

// code stored in the sketch: Level_Sensor_v2_3_sensors.ino
/*
  Level Sensor  v2 for new Board done in Fritzing
  Turns on a relais when low water level is detected and check if refill Tank is empty, to protect pump from running dry...

  using Non-contact Liquid Level Sensor XKC-Y25-T12V SKU: SEN0204
  https://www.dfrobot.com/wiki/index.php/Non-contact_Liquid_Level_Sensor_XKC-Y25-T12V_SKU:_SEN0204
  for upper level detektion and
  Liquid Level Sensor-FS-IR02 SKU: SEN0205
  https://www.dfrobot.com/wiki/index.php/Liquid_Level_Sensor-FS-IR02_SKU:_SEN0205
  for lower level detection
  
  modified 14 January 2019
  by Helmar Waiczies
*/

int Liquid_level=0;
int Liquid_level1=0;
int Liquid_level2=0;
int Liquid_levelTank=0;
int LED=LED_BUILTIN;
int Relais=2;
int SensLowTank=A1;
int SensLow=A2;
int SensHigh=A3;
// the setup function runs once when you press reset or power the board
void setup() {
  // initialize digital pin LED_BUILTIN as an output.
  pinMode(LED, OUTPUT);
  digitalWrite(LED, LOW);
  pinMode(Relais, OUTPUT);
  digitalWrite(Relais, LOW);
  Serial.begin(9600);
  pinMode(SensLowTank,INPUT); //opt. or capacitive Sensot for refill tank
  pinMode(SensLow,INPUT);  //opt. Sensor
  pinMode(SensHigh,INPUT);  //cap. or opt. sensor (overflow protection)
}

// the loop function runs over and over again forever
void loop() {
  Liquid_level1=digitalRead(SensLow);
  Liquid_level2=digitalRead(SensHigh);
  Liquid_levelTank=digitalRead(SensLowTank);
  Liquid_level=Liquid_level1+Liquid_level2;
//  Serial.print("Water_Level Low/OK = ");
//  Serial.println(Liquid_level1,DEC);
//  Serial.print("Water_Level High = ");
//  Serial.println(Liquid_level2,DEC);
//  Serial.print("Water_Tank_Level = ");
//  Serial.println(Liquid_levelTank,DEC);
  if (Liquid_level == 0) {
    if (Liquid_levelTank == 1) {
    digitalWrite(LED, HIGH);    // turn the LED on by making the voltage HIGH
    digitalWrite(Relais, HIGH);  //pumpe an
    Serial.println("Water_Level Low, refilling");
    }
  }
  if (Liquid_level == 1) {
    digitalWrite(LED, LOW);   // turn the LED OFF 
    digitalWrite(Relais, LOW);   //pumpe aus
    Serial.println("Water_Level ok");
  }
  if (Liquid_level == 2) {
    digitalWrite(LED, LOW);   // turn the LED OFF  
    digitalWrite(Relais, LOW);   //pumpe aus
    Serial.println("Water_Level to high, remove some water, possible overflow!!!");
  }
  if (Liquid_levelTank == 0) {
    digitalWrite(LED, LOW);   // turn the LED OFF  
    digitalWrite(Relais, LOW);   //pumpe aus
    Serial.println("Water_Tank_Level to low, refill Water Tank!");
  }

  delay(1000);                     // wait for a second

}
